# Fritzing sketch ldrpiezo01 (saved by Fritzing 0.7.5b)
breadboards: 1

parts:
  Arduino1 = Arduino
  J1 = Piezo Speaker
  R1 = Resistor [tolerance=±5% resistance=1k package=THT]
  R2 = Photocell (LDR) [package=THT]

nets:
  N1: Arduino1.D11, J1.pin2
  N2: Arduino1.+5V, R2.pin_0
  N3: Arduino1.GND, J1.pin1, R1.Pin_1
